# Fritzing sketch mpu6050 (saved by Fritzing 1.0.8)

parts:
  Part1 = InvenSense MPU6050
  J1 = STM32 Nucleo boards

nets:
  VCC: Part1.VCC, J1.3V3
  GND: Part1.GND, J1.GND
  N1: Part1.SCL, J1.PB6
  N2: Part1.XDA, J1.PB7
